# Fritzing sketch Summative_v3 (saved by Fritzing 0.9.3b)
breadboards: 1

parts:
  Part1 = Arduino Uno (Rev3)
  LED1 = RGB LED (com. cathode, rbg) [package="5 mm [THT]"]
  R2 = Resistor [tolerance=±5% resistance=220 package=THT]
  R3 = Resistor [tolerance=±5% resistance=220 package=THT]
  R4 = Resistor [tolerance=±5% resistance=220 package=THT]
  M1 = DC Motor
  M2 = DC Motor
  D1 = Rectifier Diode [part_number=1N4001 package="300 mil [THT]"]
  R6 = Resistor [tolerance=±5% resistance=220 package=THT]
  Q1 = NPN-Transistor [package="SOT-23 [SMD]"]
  R7 = Resistor [tolerance=±5% resistance=220 package=THT]
  D3 = Rectifier Diode [part_number=1N4001 package="300 mil [THT]"]
  Q3 = NPN-Transistor [package="SOT-23 [SMD]"]
  IR1 = TSOP312.., 314.. [package=THT]
  HC-SR04_Sensor_1 = HC-SR04 Ultrasonic Distance Sensor
  U1 = 7-SEGMENT-DISPLAY [package=7-segment-display]

nets:
  N1: Part1.A0, R2.Pin_0
  N2: Part1.A1, R3.Pin_0
  N3: Part1.A2, R4.Pin_0
  N4: Part1.D8, IR1.Data
  N5: Part1.D9_PWM, HC-SR04_Sensor_1.TRIG
  N6: Part1.D10_PWM/SS, HC-SR04_Sensor_1.GND
  N7: Part1.D11_PWM/MOSI, U1.C
  N8: Part1.D12/MISO, R6.Pin_1
  N9: Part1.D13/SCK, R7.Pin_1
  GND: Part1.GND, LED1.common_cathode, Q1.2, Q3.2, IR1.GND, HC-SR04_Sensor_1.ECHO, U1.G1, U1.G2
  N10: Part1.D1/TX, U1.D
  N11: Part1.D2, U1.E
  N12: Part1.D3_PWM, U1.B
  N13: Part1.D4, U1.A
  N14: Part1.D5_PWM, U1.F
  N15: Part1.D6_PWM, U1.DP
  N16: Part1.D7, U1.G
  5V: Part1.5V, M1.pin_1, M2.pin_1, D1.anode, D3.anode, IR1.Vs, HC-SR04_Sensor_1.VCC
  N17: LED1.red_anode, R4.Pin_1
  N18: LED1.blue_anode, R3.Pin_1
  N19: LED1.green_anode, R2.Pin_1
  N20: M1.pin_2, D3.cathode, Q3.1
  N21: M2.pin_2, D1.cathode, Q1.1
  N22: R6.Pin_0, Q1.0
  N23: R7.Pin_0, Q3.0

notes:
  Automated Walker, Dhirhan Kanesalinigam
  DC Motors
  RGB LED
  IR Receiver
  Ultrasound Sensor
  7 Segment Display
  Automated-Walker
